// Logisim project ALUcontrol_adaptada.circ as structural Verilog: 2 circuits, main circuit main
module main (
);

  ALUcontrol alucontrol_1 ();  // open: Funct, ALUOp, Jr, Operation
endmodule

module ALUcontrol (
  input  [5:0] Funct,
  input  [1:0] ALUOp,
  output Jr,
  output [2:0] Operation
);

  wire and_1_out, and_2_out, and_3_out, and_4_out, and_5_out, and_6_out, and_7_out, and_8_out, not_1_out,
       not_2_out, not_3_out, not_4_out, not_5_out, not_6_out, not_7_out, not_8_out;

  not not_1 (not_1_out, Funct[0]);
  not not_2 (not_2_out, Funct[1]);
  not not_3 (not_3_out, Funct[2]);
  not not_4 (not_4_out, Funct[3]);
  not not_5 (not_5_out, Funct[4]);
  not not_6 (not_6_out, Funct[5]);
  not not_7 (not_7_out, ALUOp[0]);
  not not_8 (not_8_out, ALUOp[1]);
  and and_1 (and_1_out, not_7_out, not_8_out);
  and and_2 (and_2_out, not_1_out, not_2_out, Funct[2], not_4_out, Funct[4], not_6_out, not_7_out);
  and and_3 (and_3_out, Funct[0], Funct[1], Funct[2], not_4_out, not_5_out, Funct[5], not_7_out);
  and and_4 (and_4_out, Funct[0], not_2_out, Funct[2], not_4_out, not_5_out, Funct[5], not_7_out, ALUOp[1]);
  and and_5 (and_5_out, not_1_out, Funct[1], not_3_out, Funct[3], not_5_out, Funct[5], not_7_out, ALUOp[1]);
  and and_6 (and_6_out, not_2_out, Funct[2], not_4_out, not_5_out, Funct[5], ALUOp[1]);
  and and_7 (and_7_out, Funct[0], Funct[2], not_4_out, not_5_out, Funct[5], ALUOp[1]);
  and and_8 (and_8_out, ALUOp[0], ALUOp[1]);
  and and_9 (Jr, not_1_out, not_2_out, not_3_out, Funct[3], not_5_out, not_6_out, not_7_out, ALUOp[1]);
  or or_1 (Operation[0], and_1_out, and_2_out, and_3_out);
  or or_2 (Operation[1], and_4_out, and_5_out);
  or or_3 (Operation[2], and_6_out, and_7_out, and_8_out);
endmodule
